// Logisim project Rounder.circ as structural Verilog: 1 circuit, main circuit main
// ROUNDER
module main (
  input  [31:0] Significand,
  output [31:0] ROUNDED_SIGNIFICANT
);

  wire and_1_out, comparator_1_eq, comparator_1_gt, or_1_out;

  Comparator #(.mode("unsigned")) comparator_1 (
    .a(Significand[7:0]), .b(8'h80), .gt(comparator_1_gt), .eq(comparator_1_eq));  // open: lt
  and and_1 (and_1_out, Significand[8], comparator_1_eq);
  Adder #(.width(24)) adder_1 (
    .a(Significand[31:8]), .b({24{1'b0}}), .out(ROUNDED_SIGNIFICANT[31:8]), .cin(or_1_out));  // open: cout
  or or_1 (or_1_out, and_1_out, comparator_1_gt);

  assign ROUNDED_SIGNIFICANT[7:0] = {8{1'b0}};
endmodule
