// Logisim project Mem_Wb_regi.circ as structural Verilog: 1 circuit, main circuit main
module main (
  input  MemToReg_RW,
  input  RW,
  input  [7:0] Data_Memory,
  input  [7:0] ALU_Result,
  input  [3:0] RD,
  input  clock,
  input  clear,
  input  clock_2,
  input  clear_2,
  output MemToReg_RW_2,
  output RW_2,
  output [7:0] Data_Memory_2,
  output [7:0] ALU_Result_2,
  output [3:0] RD_2
);

  Register #(.width(22)) register_1 (
    .D({RD, ALU_Result, Data_Memory, RW, MemToReg_RW}), .en(1'b1),
    .Q({RD_2, ALU_Result_2, Data_Memory_2, RW_2, MemToReg_RW_2}), .clk(clock), .clr(clear));
endmodule
